# Fritzing sketch Diagrama General (saved by Fritzing 0.9.3b)
breadboards: 1

parts:
  Componente1 = Arduino Uno (Rev3)
  T1 = LM35 Temperature Sensor [package="TO92 [THT]"]
  Mod1 = MQ-7 breakout
  L298N1 = L298N DC motor driver
  M3 = DC Motor
  M4 = DC Motor
  M5 = DC Motor
  M6 = DC Motor
  BAT1 = BC9VPC [package=bc9vpc]
  U1 = ESP8266 WiFi Module [part_number=ESP8266]
  ESP32_-_Back1 = ESP32 - CAM
  R1 = Resistor [tolerance=±5% resistance=220 package=THT]
  R2 = Resistor [tolerance=±5% resistance=220 package=THT]

nets:
  N1: Componente1.A0, T1.Vout
  N2: Componente1.A1, Mod1.AO
  N3: Componente1.D10_PWM/SS, Componente1.D11_PWM/MOSI, Componente1.D12/MISO, Componente1.D13/SCK, L298N1.ENA, L298N1.IN1, L298N1.IN2, L298N1.IN3, L298N1.IN4
  GND: Componente1.GND, T1.GND, Mod1.GND, L298N1.12V, L298N1.GND, BAT1.V+, BAT1.V-, U1.GND, ESP32_-_Back1.GND, R2.Pin_1
  N4: Componente1.D0/RX, ESP32_-_Back1.3.3V_/_5V_/_P_OUT
  N5: Componente1.D1/TX, ESP32_-_Back1.GPIO3_/_RX
  N6: Componente1.D4, U1.TXD
  N7: Componente1.D5_PWM, R1.Pin_0
  3V3: Componente1.3V3, U1.VCC, U1.CH_PD
  5V: Componente1.5V, T1.+Vs, Mod1.VCC, ESP32_-_Back1.5V
  N8: L298N1.OUT1, M5.pin_2, M6.pin_2
  N9: L298N1.OUT2, M5.pin_1, M6.pin_1
  N10: L298N1.OUT3, M3.pin_1, M4.pin_1
  N11: L298N1.OUT4, M3.pin_2, M4.pin_2
  N12: U1.RXD, R1.Pin_1, R2.Pin_0
  N13: ESP32_-_Back1.GPIO16, ESP32_-_Back1.GPIO0

custom parts:
  MQ-7 breakout: MQ-5 gas sensor
  L298N DC motor driver: 2x DC motor driver with 78M05 positive voltage regulator (7..35 V) L298N: max 46 V, 2 A Set 5 V Enable jumper to enable 5 V regultor (needed for the L298N) and +5 V output at screw terminal or supply external +5 V at screw terminal Set ENA and/or ENB to +5 V to enable motor permanently or supply ENA and/or ENB with PWM signal IN1 and IN2 set rotation directory for motor A (OUT1/OUT2) IN2 and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
  ESP8266 WiFi Module: Generic WiFi Module based on the ESP8266 with onboard PCB antenna and UART communications
  ESP32 - CAM: The ESP32-CAM has a very competitive small-size camera module that can operate independently as a minimum system with a footprint of only 27*40.5*4.5mm and a deep sleep current of up to 6mA.
