# Fritzing sketch ESP32-CAM (saved by Fritzing 0.9.3b)
breadboards: 1

parts:
  Componente2 = Arduino Uno (Rev3)
  ESP32_-_Back2 = ESP32 - CAM

nets:
  N1: Componente2.D0/RX, ESP32_-_Back2.3.3V_/_5V_/_P_OUT
  N2: Componente2.D1/TX, ESP32_-_Back2.GPIO3_/_RX
  5V: Componente2.5V, ESP32_-_Back2.5V
  GND: Componente2.GND, ESP32_-_Back2.GND
  N3: ESP32_-_Back2.GPIO16, ESP32_-_Back2.GPIO0

custom parts:
  ESP32 - CAM: The ESP32-CAM has a very competitive small-size camera module that can operate independently as a minimum system with a footprint of only 27*40.5*4.5mm and a deep sleep current of up to 6mA.
