# Fritzing sketch ESP8266 (saved by Fritzing 0.9.3b)
breadboards: 1

parts:
  Componente3 = Arduino Uno (Rev3)
  U3 = ESP8266 WiFi Module [part_number=ESP8266]
  R5 = Resistor [tolerance=±5% resistance=220 package=THT]
  R6 = Resistor [tolerance=±5% resistance=220 package=THT]

nets:
  N1: Componente3.D4, U3.TXD
  N2: Componente3.D5_PWM, R5.Pin_0
  3V3: Componente3.3V3, U3.VCC, U3.CH_PD
  GND: Componente3.GND, U3.GND, R6.Pin_1
  N3: U3.RXD, R5.Pin_1, R6.Pin_0

custom parts:
  ESP8266 WiFi Module: Generic WiFi Module based on the ESP8266 with onboard PCB antenna and UART communications
