# Fritzing sketch L289N (saved by Fritzing 0.9.3b)
breadboards: 1

parts:
  Componente2 = Arduino Uno (Rev3)
  M7 = DC Motor
  M8 = DC Motor
  M9 = DC Motor
  M10 = DC Motor
  L298N2 = L298N DC motor driver
  BAT2 = BC9VPC [package=bc9vpc]

nets:
  N1: Componente2.D10_PWM/SS, Componente2.D11_PWM/MOSI, Componente2.D12/MISO, Componente2.D13/SCK, L298N2.ENA, L298N2.IN1, L298N2.IN2, L298N2.IN3, L298N2.IN4
  GND: Componente2.GND, L298N2.12V, L298N2.GND, BAT2.V+, BAT2.V-
  N2: M7.pin_1, M8.pin_1, L298N2.OUT2
  N3: M7.pin_2, M8.pin_2, L298N2.OUT1
  N4: M9.pin_1, M10.pin_1, L298N2.OUT3
  N5: M9.pin_2, M10.pin_2, L298N2.OUT4

custom parts:
  L298N DC motor driver: 2x DC motor driver with 78M05 positive voltage regulator (7..35 V) L298N: max 46 V, 2 A Set 5 V Enable jumper to enable 5 V regultor (needed for the L298N) and +5 V output at screw terminal or supply external +5 V at screw terminal Set ENA and/or ENB to +5 V to enable motor permanently or supply ENA and/or ENB with PWM signal IN1 and IN2 set rotation directory for motor A (OUT1/OUT2) IN2 and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
