# Fritzing sketch LM35 (saved by Fritzing 0.9.3b)
breadboards: 1

parts:
  Componente2 = Arduino Uno (Rev3)
  T2 = LM35 Temperature Sensor [package="TO92 [THT]"]

nets:
  N1: Componente2.A0, T2.Vout
  N2: Componente2.5V, T2.+Vs
  GND: Componente2.GND, T2.GND
