# Fritzing sketch MQ2 (saved by Fritzing 0.9.3b)
breadboards: 1

parts:
  Componente2 = Arduino Uno (Rev3)
  Mod2 = MQ-7 breakout

nets:
  N1: Componente2.A1, Mod2.AO
  5V: Componente2.5V, Mod2.VCC
  GND: Componente2.GND, Mod2.GND

custom parts:
  MQ-7 breakout: MQ-5 gas sensor
